# Fritzing sketch Untitled Sketch 2 (saved by Fritzing 0.9.2b)

parts:
  U1 = TCM8240MD [package=tcm8240md]  # not connected
  Part1 = 2.4 Touchscreen TFT Breakout w:MicroSD  # not connected
  U2 = MIC [package=mic_electret_smd]
  CONN1 = USB connector [package=THT]
  J1 = Basic Servo  # not connected
  Raspberry_Pi1 = Raspberry Pi B+  # not connected
  Raspberry_Pi1_2 = Raspberry Pi 2  # not connected

nets:
  N1: U2.1, CONN1.d-
  N2: U2.2, CONN1.d+

custom parts:
  2.4 Touchscreen TFT Breakout w:MicroSD: Add some jazz & pizzazz to your project with a color touchscreen LCD. This TFT display is 2.4" diagonal with a bright (4 white-LED) backlight and it's colorful! 240x320 pixels with individual RGB pixel control, this has way more resolution than a black and white 128x64 display. As a bonus, this display has a resistive touchscreen attached to it already, so you can detect finger presses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
